# Fritzing sketch boost_station (saved by Fritzing 0.9.2b)
breadboards: 1

parts:
  Part1 = Sunny Buddy MPPT LiPo Charger
  SparkFun_ESP8266_Thing1 = SparkFun ESP8266 Thing [part_number=WRL-13231]
  BATT1 = LiPoly Battery (1300mAh)  # not connected
  J$1 = SMA Antenna Connector [package=sma-edge]  # not connected
  ANT1 = Antenna  # not connected
  J$2 = SMA Antenna Connector [package=sma-edge]  # not connected
  ANT2 = Antenna  # not connected
  Part3 = Solar Cell
  Part4 = Adafruit Feather M0 RFM9x LoRa [part_number="Adafruit #3178 or #3179"]

nets:
  N1: Part1.Secondary_+, Part3.+
  N2: Part1.Secondary_-, Part3.-
  N3: Part1.Load_+_(Screw_Terminal), Part4.VBAT, Part4.D6
  GND: Part1.Load_-_(Screw_Terminal), SparkFun_ESP8266_Thing1.GND, Part4.GND
  N4: Part1.Load_+_(.1"_Header), SparkFun_ESP8266_Thing1.VIN
  N5: SparkFun_ESP8266_Thing1.U0TXO, Part4.D0
  N6: SparkFun_ESP8266_Thing1.U0RXI, Part4.D1

custom parts:
  Sunny Buddy MPPT LiPo Charger: Switch-mode MPPT charger for single cell LiPo batteries. Accepts up to 20V solar cell input.
  SparkFun ESP8266 Thing: The SparkFun ESP8266 Thing is a breakout and development board for the ESP8266 WiFi SoC – a leading platform for Internet of Things (IoT) or WiFi-related projects. The Thing is low-cost and easy to use, and Arduino IDE integration can be achieved in just a few steps. We’ve made the ESP8266 easy to use by breaking out all of the module’s pins, adding a LiPo charger, power supply, and all of the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
  LiPoly Battery (1300mAh): Lithium Ion Polymer Battery (1300mAh)
  Adafruit Feather M0 RFM9x LoRa: This is the Adafruit Feather M0 RFM95 LoRa Radio - our take on an microcontroller with a "Long Range (LoRa)" packet radio transceiver with built in USB and battery charging. Its an Adafruit Feather M0 with a 433Mhz or 900MHz radio module cooked in! Great for making wireless networks that are more flexible than Bluetooth LE and without the high power requirements of WiFi. We have other boards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
